// Logisim project Project_final.circ as structural Verilog: 3 circuits, main circuit main
module main (
  input  in_1,
  input  in_2,
  input  in_3,
  input  in_4,
  input  in_5
);

  wire AC_INC, AC_LD, AR_LD, CLK, DR_INC, DR_LD, IR_LD, MEM_READ, MEM_WRITE, PC_INC, PC_LD;
  wire [2:0] ALU_SLCT, BUS_SLCT;
  wire [6:0] AR_q, bit_extender_1_out, bit_extender_2_out, PC_q;
  wire [15:0] AC, alu_1_ac_out, bit_extender_3_out, bit_extender_4_out, DR, IR, multiplexer_1_out,
       ram_1_data, TR_q;

  CU cu_1 (
    .IR(IR), .CLk(CLK), .DR(DR), .Read_Mem(MEM_READ), .PC_INC(PC_INC), .PC_LD(PC_LD), .DR_LD(DR_LD),
    .DR_INC(DR_INC), .IR_LD(IR_LD), .Memory_Write(MEM_WRITE), .BUS_SLCT(BUS_SLCT), .AR_LD(AR_LD),
    .ALU_SLCT(ALU_SLCT), .AC_LD(AC_LD), .AC_INC(AC_INC));
  Alu alu_1 (.AC_IN(AC), .DR(DR), .ALU_SELECT(ALU_SLCT), .AC_OUT(alu_1_ac_out));
  Bit_Extender #(.in_width(16), .out_width(7)) bit_extender_1 (.in(multiplexer_1_out), .out(bit_extender_1_out));
  Clock clock_1 (.out(CLK));
  RAM #(.addrWidth(7), .dataWidth(16), .bus("separate")) ram_1 (
    .addr(AR_q), .din(multiplexer_1_out), .data(ram_1_data), .str(MEM_WRITE), .sel(1'b1), .clk(CLK),
    .ld(MEM_READ));  // open: clr
  Bit_Extender #(.in_width(16), .out_width(7)) bit_extender_2 (.in(multiplexer_1_out), .out(bit_extender_2_out));
  Register #(.width(16)) u_IR (.D(multiplexer_1_out), .en(IR_LD), .Q(IR), .clk(CLK), .clr(in_5));
  Register #(.width(7)) AR (.D(bit_extender_1_out), .en(AR_LD), .Q(AR_q), .clk(CLK));  // open: clr
  Counter #(.width(16), .max('hffff)) u_DR (
    .load(DR_LD), .D(multiplexer_1_out), .count(DR_INC), .Q(DR), .clk(CLK), .clr(in_1));  // open: carry
  Counter #(.width(16), .max('hffff)) u_AC (
    .load(AC_LD), .D(alu_1_ac_out), .count(AC_INC), .Q(AC), .clk(CLK), .clr(in_2));  // open: carry
  Register #(.width(16)) TR (.D(multiplexer_1_out), .en(in_3), .Q(TR_q), .clk(CLK));  // open: clr
  Counter #(.width(7), .max('h7f)) PC (
    .load(PC_LD), .D(bit_extender_2_out), .count(PC_INC), .Q(PC_q), .clk(CLK), .clr(in_4));  // open: carry
  assign bit_extender_3_out = {{9{1'b0}}, AR_q};  // Bit_Extender bit_extender_3
  assign bit_extender_4_out = {{9{1'b0}}, PC_q};  // Bit_Extender bit_extender_4
  Multiplexer #(.select(3), .width(16), .enable("false")) multiplexer_1 (
    .in0(AC), .in1(DR), .in2(TR_q), .in3(bit_extender_3_out), .in4(ram_1_data), .in5(bit_extender_4_out),
    .in6(IR), .out(multiplexer_1_out), .sel(BUS_SLCT));  // open: in7
endmodule

// ALU
module Alu (
  input  [15:0] AC_IN,
  input  [2:0] ALU_SELECT,
  input  [15:0] DR,
  output [15:0] AC_OUT
);

  wire [15:0] adder_1_out, adder_2_out, AND_out, multiplier_1_out, OR_out, subtractor_1_out;

  Adder #(.width(16)) adder_1 (.a(DR), .b(AC_IN), .out(adder_1_out), .cin(1'b0));  // open: cout
  Subtractor #(.width(16)) subtractor_1 (.a(DR), .b(AC_IN), .out(subtractor_1_out), .bin(1'b0));  // open: bout
  Multiplier #(.width(16)) multiplier_1 (.a(DR), .b(AC_IN), .out(multiplier_1_out), .cin({16{1'b0}}));  // open: cout
  Adder #(.width(16)) adder_2 (.a(DR), .b(16'h1), .out(adder_2_out), .cin(1'b0));  // open: cout
  assign OR_out = DR | AC_IN;  // OR_Gate OR, 16 bits wide
  assign AND_out = DR & AC_IN;  // AND_Gate AND, 16 bits wide
  Multiplexer #(.select(3), .width(16), .enable("false")) multiplexer_1 (
    .in1(DR), .in2(adder_1_out), .in3(subtractor_1_out), .in4(multiplier_1_out), .in5(adder_2_out),
    .in6(OR_out), .in7(AND_out), .out(AC_OUT), .sel(ALU_SELECT));  // open: in0
endmodule

// Control Unit
module CU (
  input  [15:0] IR,
  input  CLk,
  input  [15:0] DR,
  output IR_LD,
  output Memory_Write,
  output Read_Mem,
  output [2:0] BUS_SLCT,
  output AR_LD,
  output PC_INC,
  output PC_LD,
  output DR_LD,
  output DR_INC,
  output [2:0] ALU_SLCT,
  output AC_LD,
  output AC_INC
);

  wire and_1_out, and_2_out, and_3_out, and_4_out, and_5_out, and_6_out, and_7_out, and_8_out, and_9_out,
       and_10_out, and_11_out, and_12_out, and_13_out, and_14_out, and_15_out, and_16_out, and_17_out,
       and_18_out, and_19_out, and_20_out, and_21_out, and_22_out, and_23_out, and_24_out, and_25_out,
       and_26_out, and_28_out, and_29_out, and_30_out, and_31_out, and_32_out, and_33_out, and_34_out,
       and_35_out, and_36_out, and_37_out, and_38_out, and_39_out, and_40_out, and_41_out, D0, D1, D2, D3,
       D4, D5, D6, D7, d_ff_1_q, I, not_1_out, not_2_out, not_3_out, or_1_out, or_3_out, or_6_out, or_7_out,
       or_9_out, or_11_out, or_12_out, SC_CLR, T0, T1, T2, T3, T4, T5, T6, T7, T8, T9, T10, T11, T12, T13,
       T14, T15, ZERO_DR;
  wire [3:0] SC_q;

  not not_1 (not_1_out, D7);
  not not_2 (not_2_out, D7);
  not not_3 (not_3_out, d_ff_1_q);
  D_Flip_Flop d_ff_1 (.clk(CLk), .D(SC_CLR), .Q(d_ff_1_q));  // open: Qn, preset, en, reset
  or or_1 (or_1_out, D0, D1, D2, D3);
  buf or_2 (IR_LD, T1);  // OR_Gate
  or or_3 (or_3_out, D0, D1, D2, D3, D6);
  Decoder #(.select(4), .enable("false")) decoder_1 (
    .out0(T0), .out1(T1), .out2(T2), .out3(T3), .out4(T4), .out5(T5), .out6(T6), .out7(T7), .out8(T8),
    .out9(T9), .out10(T10), .out11(T11), .out12(T12), .out13(T13), .out14(T14), .out15(T15), .sel(SC_q));
  Counter #(.width(4), .max('hf)) SC (.count(not_3_out), .Q(SC_q), .clk(CLk), .clr(d_ff_1_q));  // open: load, D, carry
  and and_1 (and_1_out, T3, not_2_out, I);
  and and_2 (and_2_out, T5, D0);
  and and_3 (and_3_out, T5, D1);
  and and_4 (and_4_out, T6, D1);
  and and_5 (and_5_out, T5, D2);
  and and_6 (and_6_out, T5, D3);
  and and_7 (and_7_out, T6, D1);
  and and_8 (and_8_out, T4, or_3_out);
  and and_9 (and_9_out, T3, not_1_out, I);
  and and_10 (and_10_out, T5, or_1_out);
  or or_4 (Read_Mem, T1, and_1_out, and_8_out);
  and and_11 (and_11_out, T4, D4);
  or or_5 (AR_LD, T0, T2, and_9_out);
  or or_6 (or_6_out, D0, D2, D3);
  or or_7 (or_7_out, D4, D5);
  and and_12 (and_12_out, T5, D1);
  and and_13 (and_13_out, T5, D0);
  and and_14 (and_14_out, T6, D1);
  and and_15 (and_15_out, T5, D2);
  and and_16 (and_16_out, T5, D3);
  and and_17 (and_17_out, T4, D4);
  and and_18 (and_18_out, T4, D5);
  and and_19 (and_19_out, T3, D7);
  and and_20 (and_20_out, T5, or_6_out);
  and and_21 (and_21_out, T4, or_7_out);
  and and_22 (and_22_out, T3, D7);
  and and_23 (and_23_out, T6, D1);
  and and_24 (and_24_out, T6, D6);
  or or_8 (AC_LD, and_2_out, and_3_out, and_4_out, and_5_out, and_6_out, and_10_out, and_7_out);
  or or_9 (or_9_out, and_12_out, and_11_out);
  and and_25 (and_25_out, T6, D6);
  and and_26 (and_26_out, T4, D5);
  and and_27 (AC_INC, T3, D7);
  Priority_Encoder priority_encoder_1 (
    .in0(or_9_out), .in1(and_25_out), .in2(1'b0), .in3(and_26_out), .in4(Read_Mem), .in5(T0), .in6(T2),
    .in7(1'b0), .out(BUS_SLCT));  // open: en_in, gs, en_out
  or or_10 (SC_CLR, and_13_out, and_14_out, and_15_out, and_16_out, and_17_out, and_18_out, and_19_out, and_20_out, and_21_out, and_22_out, and_23_out, and_24_out);
  Decoder #(.select(3), .enable("false")) decoder_2 (
    .out0(D0), .out1(D1), .out2(D2), .out3(D3), .out4(D4), .out5(D5), .out6(D6), .out7(D7), .sel(IR[14:12]));
  D_Flip_Flop u_I (.clk(CLk), .D(IR[15]), .Q(I));  // open: Qn, preset, en, reset
  or or_11 (or_11_out, D1, D3);
  and and_28 (and_28_out, T5, D2);
  and and_29 (and_29_out, T6, D6, ZERO_DR);
  or or_12 (or_12_out, D0, D1, D2, D3, D5);
  and and_30 (and_30_out, T5, D0);
  and and_31 (and_31_out, T6, D1);
  and and_32 (and_32_out, or_11_out, T5);
  and and_33 (and_33_out, T4, D4);
  and and_34 (and_34_out, T6, D6);
  and and_35 (and_35_out, T4, or_12_out);
  and and_36 (and_36_out, T5, D1);
  nor nor_1 (ZERO_DR, DR[0], DR[1], DR[2], DR[3], DR[4], DR[5], DR[6], DR[7], DR[8], DR[9], DR[10], DR[11], DR[12], DR[13], DR[14], DR[15]);
  or or_13 (Memory_Write, and_33_out, and_34_out);
  and and_37 (and_37_out, D6, T5);
  and and_38 (and_38_out, D0, T4);
  and and_39 (and_39_out, D6, T4);
  and and_40 (and_40_out, D1, T4);
  and and_41 (and_41_out, D3, T4);
  Priority_Encoder priority_encoder_2 (
    .in0(1'b1), .in1(and_32_out), .in2(and_30_out), .in3(and_31_out), .in4(and_28_out), .in5(1'b0),
    .in6(1'b0), .in7(1'b0), .out(ALU_SLCT));  // open: en_in, gs, en_out
  and and_42 (PC_LD, T4, D5);
  or or_14 (PC_INC, T1, and_29_out);
  or or_15 (DR_LD, and_38_out, and_37_out, and_35_out, and_36_out, and_39_out, and_40_out, and_41_out);
  and and_43 (DR_INC, T5, D6);

  // Notes on the sheet:
  //   T4
  //   T6
  //   D6
endmodule
